# Fritzing sketch Tool Lockout v1.3 (saved by Fritzing 0.8.0b)
breadboards: 1

parts:
  Ethernet = WIZ820io [part_number=WIZ820io]
  Vcc_Ctr_Pos = Power plug
  C1 = Ceramic Capacitor [capacitance=10µF package="100 mil [THT, multilayer]"]
  +5Vreg = Voltage Regulator - 5V [package="TO220 [THT]"]
  +3_3Vreg = Voltage Regulator - 3.3V [package="TO220 [THT]"]
  C2 = Ceramic Capacitor [capacitance=10µF package="100 mil [THT, multilayer]"]
  C3 = Ceramic Capacitor [capacitance=10µF package="100 mil [THT, multilayer]"]
  N-Chnl_FET_(D4) = Basic FET N-Channel [package="TO220 [THT]"]
  ICSP = mystery part, 6 pins [chip_label=ICSP spacing=100mil]
  Reset = Pushbutton [package="[THT]"]
  D1 = Rectifier Diode [part_number=1N4004 package="300 mil [THT]"]
  RED_D5 = LED - 3mm [color="Red (633nm)" package="3 mm [THT]"]
  GRN_D6 = LED - 3mm [color="Green (565nm)" package="3 mm [THT]"]
  R2 = Resistor [tolerance=±5% resistance=1M package=THT]
  RFID = male pin header, 4 pins [form="♂ (male)"]
  Vio = male pin header, 3 pins [form="♂ (male)"]
  16MHz = Resonator [frequency="16 Mhz" package=THT]
  C8 = Electrolytic Capacitor [capacitance=47µF voltage=50V package="100 mil [THT, electrolytic]"]
  E-Stop = male pin header, 2 pins [form="♂ (male)"]
  R1 = Resistor [tolerance=±5% resistance=10k package=THT]
  D2 = Rectifier Diode [part_number=1N4004 package="300 mil [THT]"]
  C6 = Ceramic Capacitor [capacitance=0.1µF voltage=50V package="100 mil [THT, multilayer]"]
  C7 = Ceramic Capacitor [capacitance=100pF voltage=50V package="100 mil [THT, multilayer]"]
  C5 = Ceramic Capacitor [capacitance=0.1µF voltage=50V package="100 mil [THT, multilayer]"]
  R3 = Resistor [tolerance=±5% resistance=10k package=THT]
  D7_D8 = male pin header, 4 pins [form="♂ (male)"]
  MoSFET_Output_(D4) = screw terminal, 2 pins
  EN_Rst = male pin header, 3 pins [form="♂ (male)"]
  AREF_A0_A1_A2_A3_A4_A5 = male pin header, 7 pins [form="♂ (male)"]
  Atmega328p = atmega168 [package="DIP28 [THT]"]
  C4 = Ceramic Capacitor [capacitance=10µF package="100 mil [THT, multilayer]"]
  FTDI = male pin header, 6 pins [form="♂ (male)"]

nets:
  GND: Ethernet.GND, Vcc_Ctr_Pos.GND, C1.0, +5Vreg.GND, +3_3Vreg.GND, C2.1, C3.1, N-Chnl_FET_(D4).source, ICSP.pin4, Reset.Pin_3, Reset.Pin_4, RED_D5.cathode, GRN_D6.cathode, RFID.pin1, Vio.pin2, 16MHz.GND, C8.-, E-Stop.pin2, R1.Pin_1, C6.0, C7.0, D7_D8.pin1, Atmega328p.Pin_8, Atmega328p.Pin_22, C4.1, FTDI.pin1
  N1: Ethernet.MOSI, ICSP.pin5, Atmega328p.Pin_17
  N2: Ethernet.SCLK, ICSP.pin2, Atmega328p.Pin_19
  N3: Ethernet.nSS, Atmega328p.Pin_16
  N4: Ethernet.nINT, Atmega328p.Pin_5
  N5: Ethernet.MISO, ICSP.pin1, Atmega328p.Pin_18
  N6: Ethernet.nRESET, EN_Rst.pin2
  N7: Ethernet.PWDN, Atmega328p.Pin_15
  3.3V: Ethernet.VIN, +3_3Vreg.output_voltage, C2.0, Vio.pin3
  N8: Vcc_Ctr_Pos.VCC, D2.anode
  5V: C1.1, +5Vreg.output_voltage, +3_3Vreg.input_voltage, C3.0, ICSP.pin6, RFID.pin4, Vio.pin1, C5.0, R3.Pin_0, R3.Pin_1, D7_D8.pin4, Atmega328p.Pin_7, Atmega328p.Pin_20, C4.0, FTDI.pin3, FTDI.pin6
  12V: +5Vreg.input_voltage, D1.cathode, C8.+, D2.cathode, C6.1, C7.1, MoSFET_Output_(D4).pin1
  N9: N-Chnl_FET_(D4).gate, R1.Pin_0, Atmega328p.Pin_6
  N10: N-Chnl_FET_(D4).drain, D1.anode, MoSFET_Output_(D4).pin2
  Sys_Reset: ICSP.pin3, Reset.Pin_1, Reset.Pin_2, C5.1, EN_Rst.pin1, Atmega328p.Pin_1
  N11: RED_D5.anode, Atmega328p.Pin_11
  N12: GRN_D6.anode, Atmega328p.Pin_12
  N13: R2.Pin_0, 16MHz.0, Atmega328p.Pin_9
  N14: R2.Pin_1, 16MHz.pin_1, Atmega328p.Pin_10
  N15: RFID.pin2, Atmega328p.Pin_2, FTDI.pin4
  N16: RFID.pin3, Atmega328p.Pin_3, FTDI.pin5
  N17: E-Stop.pin1, Atmega328p.Pin_4
  N18: D7_D8.pin2, Atmega328p.Pin_14
  N19: D7_D8.pin3, EN_Rst.pin3, Atmega328p.Pin_13
  N20: AREF_A0_A1_A2_A3_A4_A5.pin1, Atmega328p.Pin_21
  N21: AREF_A0_A1_A2_A3_A4_A5.pin2, Atmega328p.Pin_23
  N22: AREF_A0_A1_A2_A3_A4_A5.pin3, Atmega328p.Pin_24
  N23: AREF_A0_A1_A2_A3_A4_A5.pin4, Atmega328p.Pin_25
  N24: AREF_A0_A1_A2_A3_A4_A5.pin5, Atmega328p.Pin_26
  N25: AREF_A0_A1_A2_A3_A4_A5.pin6, Atmega328p.Pin_27
  N26: AREF_A0_A1_A2_A3_A4_A5.pin7, Atmega328p.Pin_28

notes:
  GND
  RX
  TX
  +5V
  Vcc
  Designed by Lawrence "Lemming" Dixon
  Lemelec.org/SNARC
  +3V3
  1
  S
  H
  B
  N
  E
  SNARC 
  Soft Serial RFID
  D2
  Simple NetworkAble
  RFID Controller
  V1.3 PTH
  "Don't turn it on, take it apart!"
  D7
  Rst
  SNARC
